// Digital circuit 1_1 SRAM.dig as structural Verilog
module _1_1_SRAM (
  input  Read_Sel_1,
  input  Read_Sel_2,
  input  Write_data,
  input  Write_Select,
  input  Clock,
  output Read_Data_1,
  output Read_Data_2
);

  wire d_ff_1_q, multiplexer_1_out;

  Multiplexer multiplexer_1 (.sel(Write_Select), .in_0(d_ff_1_q), .in_1(Write_data), .out(multiplexer_1_out));
  D_FF d_ff_1 (.D(multiplexer_1_out), .C(Clock), .Q(d_ff_1_q));  // open: nQ
  and and_1 (Read_Data_1, Read_Sel_1, d_ff_1_q);
  and and_2 (Read_Data_2, Read_Sel_2, d_ff_1_q);
endmodule
