// Digital circuit 1_18 SRAM.dig as structural Verilog
module _1_18_SRAM (
  input  RS_1,
  input  RS_2,
  input  WS,
  input  [17:0] WD_17_0,
  input  Clock,
  output [17:0] RD_1,
  output [17:0] RD_2
);

  _1_1_SRAM _1_1_sram_1 (
    .Read_Sel_1(RS_1), .Read_Sel_2(RS_2), .Write_data(WD_17_0[0]), .Write_Select(WS), .Clock(Clock),
    .Read_Data_1(RD_1[0]), .Read_Data_2(RD_2[0]));
  _1_1_SRAM _1_1_sram_2 (
    .Read_Sel_1(RS_1), .Read_Sel_2(RS_2), .Write_data(WD_17_0[1]), .Write_Select(WS), .Clock(Clock),
    .Read_Data_1(RD_1[1]), .Read_Data_2(RD_2[1]));
  _1_1_SRAM _1_1_sram_3 (
    .Read_Sel_1(RS_1), .Read_Sel_2(RS_2), .Write_data(WD_17_0[3]), .Write_Select(WS), .Clock(Clock),
    .Read_Data_1(RD_1[3]), .Read_Data_2(RD_2[3]));
  _1_1_SRAM _1_1_sram_4 (
    .Read_Sel_1(RS_1), .Read_Sel_2(RS_2), .Write_data(WD_17_0[2]), .Write_Select(WS), .Clock(Clock),
    .Read_Data_1(RD_1[2]), .Read_Data_2(RD_2[2]));
  _1_1_SRAM _1_1_sram_5 (
    .Read_Sel_1(RS_1), .Read_Sel_2(RS_2), .Write_data(WD_17_0[4]), .Write_Select(WS), .Clock(Clock),
    .Read_Data_1(RD_1[4]), .Read_Data_2(RD_2[4]));
  _1_1_SRAM _1_1_sram_6 (
    .Read_Sel_1(RS_1), .Read_Sel_2(RS_2), .Write_data(WD_17_0[5]), .Write_Select(WS), .Clock(Clock),
    .Read_Data_1(RD_1[5]), .Read_Data_2(RD_2[5]));
  _1_1_SRAM _1_1_sram_7 (
    .Read_Sel_1(RS_1), .Read_Sel_2(RS_2), .Write_data(WD_17_0[6]), .Write_Select(WS), .Clock(Clock),
    .Read_Data_1(RD_1[6]), .Read_Data_2(RD_2[6]));
  _1_1_SRAM _1_1_sram_8 (
    .Read_Sel_1(RS_1), .Read_Sel_2(RS_2), .Write_data(WD_17_0[7]), .Write_Select(WS), .Clock(Clock),
    .Read_Data_1(RD_1[7]), .Read_Data_2(RD_2[7]));
  _1_1_SRAM _1_1_sram_9 (
    .Read_Sel_1(RS_1), .Read_Sel_2(RS_2), .Write_data(WD_17_0[8]), .Write_Select(WS), .Clock(Clock),
    .Read_Data_1(RD_1[8]), .Read_Data_2(RD_2[8]));
  _1_1_SRAM _1_1_sram_10 (
    .Read_Sel_1(RS_1), .Read_Sel_2(RS_2), .Write_data(WD_17_0[9]), .Write_Select(WS), .Clock(Clock),
    .Read_Data_1(RD_1[9]), .Read_Data_2(RD_2[9]));
  _1_1_SRAM _1_1_sram_11 (
    .Read_Sel_1(RS_1), .Read_Sel_2(RS_2), .Write_data(WD_17_0[10]), .Write_Select(WS), .Clock(Clock),
    .Read_Data_1(RD_1[10]), .Read_Data_2(RD_2[10]));
  _1_1_SRAM _1_1_sram_12 (
    .Read_Sel_1(RS_1), .Read_Sel_2(RS_2), .Write_data(WD_17_0[11]), .Write_Select(WS), .Clock(Clock),
    .Read_Data_1(RD_1[11]), .Read_Data_2(RD_2[11]));
  _1_1_SRAM _1_1_sram_13 (
    .Read_Sel_1(RS_1), .Read_Sel_2(RS_2), .Write_data(WD_17_0[12]), .Write_Select(WS), .Clock(Clock),
    .Read_Data_1(RD_1[12]), .Read_Data_2(RD_2[12]));
  _1_1_SRAM _1_1_sram_14 (
    .Read_Sel_1(RS_1), .Read_Sel_2(RS_2), .Write_data(WD_17_0[13]), .Write_Select(WS), .Clock(Clock),
    .Read_Data_1(RD_1[13]), .Read_Data_2(RD_2[13]));
  _1_1_SRAM _1_1_sram_15 (
    .Read_Sel_1(RS_1), .Read_Sel_2(RS_2), .Write_data(WD_17_0[14]), .Write_Select(WS), .Clock(Clock),
    .Read_Data_1(RD_1[14]), .Read_Data_2(RD_2[14]));
  _1_1_SRAM _1_1_sram_16 (
    .Read_Sel_1(RS_1), .Read_Sel_2(RS_2), .Write_data(WD_17_0[15]), .Write_Select(WS), .Clock(Clock),
    .Read_Data_1(RD_1[15]), .Read_Data_2(RD_2[15]));
  _1_1_SRAM _1_1_sram_17 (
    .Read_Sel_1(RS_1), .Read_Sel_2(RS_2), .Write_data(WD_17_0[16]), .Write_Select(WS), .Clock(Clock),
    .Read_Data_1(RD_1[16]), .Read_Data_2(RD_2[16]));
  _1_1_SRAM _1_1_sram_18 (
    .Read_Sel_1(RS_1), .Read_Sel_2(RS_2), .Write_data(WD_17_0[17]), .Write_Select(WS), .Clock(Clock),
    .Read_Data_1(RD_1[17]), .Read_Data_2(RD_2[17]));

  // Other names for the same wires on the sheet: RD1_0 = RD_1[0]; RD1_1 = RD_1[1]; RD1_2 = RD_1[2]; RD1_3 = RD_1[3];
  //   RD1_4 = RD_1[4]; RD1_5 = RD_1[5]; RD1_6 = RD_1[6]; RD1_7 = RD_1[7]; RD1_8 = RD_1[8]; RD1_9 = RD_1[9];
  //   RD1_10 = RD_1[10]; RD1_11 = RD_1[11]; RD1_12 = RD_1[12]; RD1_13 = RD_1[13]; RD1_14 = RD_1[14];
  //   RD1_15 = RD_1[15]; RD1_16 = RD_1[16]; RD1_17 = RD_1[17]; RD2_0 = RD_2[0]; RD2_1 = RD_2[1]; RD2_2 = RD_2[2];
  //   RD2_3 = RD_2[3]; RD2_4 = RD_2[4]; RD2_5 = RD_2[5]; RD2_6 = RD_2[6]; RD2_7 = RD_2[7]; RD2_8 = RD_2[8];
  //   RD2_9 = RD_2[9]; RD2_10 = RD_2[10]; RD2_11 = RD_2[11]; RD2_12 = RD_2[12]; RD2_13 = RD_2[13]; RD2_14 = RD_2[14];
  //   RD2_15 = RD_2[15]; RD2_16 = RD_2[16]; RD2_17 = RD_2[17]
endmodule
