// Digital circuit 1_bit_reg.dig as structural Verilog
module _1_bit_reg (
  input  D_in,
  input  Sel,
  input  Clock,
  output D_out
);

  wire multiplexer_1_out;

  Multiplexer multiplexer_1 (.sel(Sel), .in_0(D_out), .in_1(D_in), .out(multiplexer_1_out));
  D_FF d_ff_1 (.D(multiplexer_1_out), .C(Clock), .Q(D_out));  // open: nQ
endmodule
