// Digital circuit 3 bit PC adder.dig as structural Verilog
module _3_bit_PC_adder (
  input  [2:0] I_2_0,
  output [2:0] O_2_0
);

  wire [4:3] _5_bit_adder_1_s_4_0;

  _5_bit_adder _5_bit_adder_1 (
    .X_4_0({2'b00, I_2_0}), .Y_4_0(5'b00001), .Cin(1'b0), .S_4_0({_5_bit_adder_1_s_4_0, O_2_0}));  // open: Cout
endmodule
