// Digital circuit 3 bit program counter.dig as structural Verilog
module _3_bit_program_counter (
  input  [2:0] I_2_0,
  input  Sel,
  input  Clock,
  output [2:0] O_2_0
);

  wire [4:3] _5_bit_reg_1_d_out_4_0;

  _5_bit_reg _5_bit_reg_1 (
    .D_in_4_0({2'b00, I_2_0}), .Sel(Sel), .Clock(Clock), .D_out_4_0({_5_bit_reg_1_d_out_4_0, O_2_0}));
  // also tied to GND on the sheet: {_5_bit_reg_1_d_out_4_0[3], _5_bit_reg_1_d_out_4_0[4]}
endmodule
