// Digital circuit 5_bit_ALU.dig as structural Verilog
module _5_bit_ALU (
  input  [4:0] A_4_0,
  input  [4:0] B_4_0,
  input  [1:0] OP_1_0,
  output [4:0] R_4_0,
  output Zero_flag,
  output Carry_flag,
  output Sign_flag
);

  wire [4:0] ADD, SHL, XOR;

  _5_bit_adder _5_bit_adder_1 (.X_4_0(A_4_0), .Y_4_0(B_4_0), .Cin(1'b0), .Cout(Carry_flag), .S_4_0(ADD));
  _5_bit_XOR _5_bit_xor_1 (.X_4_0(A_4_0), .Y_4_0(B_4_0), .O_4_0(XOR));
  SHL shl_1 (.A_4_0(A_4_0), .shift_3_0(B_4_0[2:0]), .O_4_0(SHL));
  Multiplexer #(.Selector_Bits(2), .Bits(5)) multiplexer_1 (
    .sel(OP_1_0), .in_0(ADD), .in_1(XOR), .in_2(SHL), .in_3({5{1'b0}}), .out(R_4_0));
  nor nor_1 (Zero_flag, R_4_0[0], R_4_0[1], R_4_0[2], R_4_0[3], R_4_0[4]);

  assign Sign_flag = R_4_0[4];

  // Other names for the same wires on the sheet: A[4:0] = A_4_0; B[4:0] = B_4_0; Shift[2:0] = B_4_0[2:0]
endmodule
