// Digital circuit 5_bit_XOR.dig as structural Verilog
module _5_bit_XOR (
  input  [4:0] X_4_0,
  input  [4:0] Y_4_0,
  output [4:0] O_4_0
);

  xor xor_1 (O_4_0[0], X_4_0[0], Y_4_0[0]);
  xor xor_2 (O_4_0[1], X_4_0[1], Y_4_0[1]);
  xor xor_3 (O_4_0[2], X_4_0[2], Y_4_0[2]);
  xor xor_4 (O_4_0[3], X_4_0[3], Y_4_0[3]);
  xor xor_5 (O_4_0[4], X_4_0[4], Y_4_0[4]);
endmodule
