// Digital circuit 5_bit_adder.dig as structural Verilog
module _5_bit_adder (
  input  [4:0] X_4_0,
  input  [4:0] Y_4_0,
  input  Cin,
  output Cout,
  output [4:0] S_4_0
);

  wire full_adder_2_cout, full_adder_3_cout, full_adder_4_cout, full_adder_5_cout;

  Full_adder full_adder_1 (.X(X_4_0[4]), .Y(Y_4_0[4]), .Cin(full_adder_2_cout), .S(S_4_0[4]), .Cout(Cout));
  Full_adder full_adder_2 (.X(X_4_0[3]), .Y(Y_4_0[3]), .Cin(full_adder_3_cout), .S(S_4_0[3]), .Cout(full_adder_2_cout));
  Full_adder full_adder_3 (.X(X_4_0[2]), .Y(Y_4_0[2]), .Cin(full_adder_4_cout), .S(S_4_0[2]), .Cout(full_adder_3_cout));
  Full_adder full_adder_4 (.X(X_4_0[1]), .Y(Y_4_0[1]), .Cin(full_adder_5_cout), .S(S_4_0[1]), .Cout(full_adder_4_cout));
  Full_adder full_adder_5 (.X(X_4_0[0]), .Y(Y_4_0[0]), .Cin(Cin), .S(S_4_0[0]), .Cout(full_adder_5_cout));
endmodule
