// Digital circuit 5_bit_reg.dig as structural Verilog
module _5_bit_reg (
  input  [4:0] D_in_4_0,
  input  Sel,
  input  Clock,
  output [4:0] D_out_4_0
);

  _1_bit_reg _1_bit_reg_1 (.D_in(D_in_4_0[0]), .Sel(Sel), .Clock(Clock), .D_out(D_out_4_0[0]));
  _1_bit_reg _1_bit_reg_2 (.D_in(D_in_4_0[1]), .Sel(Sel), .Clock(Clock), .D_out(D_out_4_0[1]));
  _1_bit_reg _1_bit_reg_3 (.D_in(D_in_4_0[2]), .Sel(Sel), .Clock(Clock), .D_out(D_out_4_0[2]));
  _1_bit_reg _1_bit_reg_4 (.D_in(D_in_4_0[3]), .Sel(Sel), .Clock(Clock), .D_out(D_out_4_0[3]));
  _1_bit_reg _1_bit_reg_5 (.D_in(D_in_4_0[4]), .Sel(Sel), .Clock(Clock), .D_out(D_out_4_0[4]));
endmodule
