// Digital circuit 5_bit_reg_with_4_reg.dig as structural Verilog
module _5_bit_reg_with_4_reg (
  input  [1:0] Ra_1_0,
  input  [1:0] Rb_1_0,
  input  [1:0] Wr_1_0,
  input  [4:0] Wrd_4_0,
  input  WE,
  input  Clock,
  output [4:0] A_4_0,
  output [4:0] B_4_0
);

  wire reg0, reg1, reg2, reg3;
  wire [4:0] R0, R1, R2, R3;

  Demultiplexer #(.Selector_Bits(2)) demultiplexer_1 (
    .sel(Wr_1_0), .in(WE), .out_0(reg0), .out_1(reg1), .out_2(reg2), .out_3(reg3));
  _5_bit_reg _5_bit_reg_1 (.D_in_4_0(Wrd_4_0), .Sel(reg0), .Clock(Clock), .D_out_4_0(R0));
  _5_bit_reg _5_bit_reg_2 (.D_in_4_0(Wrd_4_0), .Sel(reg1), .Clock(Clock), .D_out_4_0(R1));
  _5_bit_reg _5_bit_reg_3 (.D_in_4_0(Wrd_4_0), .Sel(reg2), .Clock(Clock), .D_out_4_0(R2));
  _5_bit_reg _5_bit_reg_4 (.D_in_4_0(Wrd_4_0), .Sel(reg3), .Clock(Clock), .D_out_4_0(R3));
  Multiplexer #(.Selector_Bits(2), .Bits(5)) multiplexer_1 (
    .sel(Ra_1_0), .in_0(R0), .in_1(R1), .in_2(R2), .in_3(R3), .out(A_4_0));
  Multiplexer #(.Selector_Bits(2), .Bits(5)) multiplexer_2 (
    .sel(Rb_1_0), .in_0(R0), .in_1(R1), .in_2(R2), .in_3(R3), .out(B_4_0));
endmodule
