// Digital circuit 7_18 SRAM.dig as structural Verilog
module _7_18_SRAM (
  input  [2:0] RA1_2_0,
  input  [2:0] RA2_2_0,
  input  [2:0] WA_2_0,
  input  [17:0] WD_17_0,
  input  WE,
  input  Clock,
  output [17:0] RD1_17_0,
  output [17:0] RD2_17_0
);

  wire RA1_0, RA1_1, RA1_2, RA1_3, RA1_4, RA1_5, RA1_6, RA2_0, RA2_1, RA2_2, RA2_3, RA2_4, RA2_5, RA2_6,
       WA_0, WA_1, WA_2, WA_3, WA_4, WA_5, WA_6;
  wire [17:0] _1_18_sram_1_rd_1, _1_18_sram_1_rd_2, _1_18_sram_2_rd_1, _1_18_sram_2_rd_2, _1_18_sram_3_rd_1,
       _1_18_sram_3_rd_2, _1_18_sram_4_rd_1, _1_18_sram_4_rd_2, _1_18_sram_5_rd_1, _1_18_sram_5_rd_2,
       _1_18_sram_6_rd_1, _1_18_sram_6_rd_2, _1_18_sram_7_rd_1, _1_18_sram_7_rd_2;

  Demultiplexer #(.Selector_Bits(3)) demultiplexer_1 (
    .sel(WA_2_0), .in(WE), .out_0(WA_0), .out_1(WA_1), .out_2(WA_2), .out_3(WA_3), .out_4(WA_4),
    .out_5(WA_5), .out_6(WA_6));  // open: out_7
  Decoder #(.Selector_Bits(3)) decoder_1 (
    .sel(RA1_2_0), .out_0(RA1_0), .out_1(RA1_1), .out_2(RA1_2), .out_3(RA1_3), .out_4(RA1_4), .out_5(RA1_5),
    .out_6(RA1_6));  // open: out_7
  Decoder #(.Selector_Bits(3)) decoder_2 (
    .sel(RA2_2_0), .out_0(RA2_0), .out_1(RA2_1), .out_2(RA2_2), .out_3(RA2_3), .out_4(RA2_4), .out_5(RA2_5),
    .out_6(RA2_6));  // open: out_7
  _1_18_SRAM _1_18_sram_1 (
    .RS_1(RA1_0), .RS_2(RA2_0), .WS(WA_0), .WD_17_0(WD_17_0), .Clock(Clock), .RD_1(_1_18_sram_1_rd_1),
    .RD_2(_1_18_sram_1_rd_2));
  _1_18_SRAM _1_18_sram_2 (
    .RS_1(RA1_1), .RS_2(RA2_1), .WS(WA_1), .WD_17_0(WD_17_0), .Clock(Clock), .RD_1(_1_18_sram_2_rd_1),
    .RD_2(_1_18_sram_2_rd_2));
  _1_18_SRAM _1_18_sram_3 (
    .RS_1(RA1_2), .RS_2(RA2_2), .WS(WA_2), .WD_17_0(WD_17_0), .Clock(Clock), .RD_1(_1_18_sram_3_rd_1),
    .RD_2(_1_18_sram_3_rd_2));
  _1_18_SRAM _1_18_sram_4 (
    .RS_1(RA1_3), .RS_2(RA2_3), .WS(WA_3), .WD_17_0(WD_17_0), .Clock(Clock), .RD_1(_1_18_sram_4_rd_1),
    .RD_2(_1_18_sram_4_rd_2));
  _1_18_SRAM _1_18_sram_5 (
    .RS_1(RA1_4), .RS_2(RA2_4), .WS(WA_4), .WD_17_0(WD_17_0), .Clock(Clock), .RD_1(_1_18_sram_5_rd_1),
    .RD_2(_1_18_sram_5_rd_2));
  _1_18_SRAM _1_18_sram_6 (
    .RS_1(RA1_5), .RS_2(RA2_5), .WS(WA_5), .WD_17_0(WD_17_0), .Clock(Clock), .RD_1(_1_18_sram_6_rd_1),
    .RD_2(_1_18_sram_6_rd_2));
  _1_18_SRAM _1_18_sram_7 (
    .RS_1(RA1_6), .RS_2(RA2_6), .WS(WA_6), .WD_17_0(WD_17_0), .Clock(Clock), .RD_1(_1_18_sram_7_rd_1),
    .RD_2(_1_18_sram_7_rd_2));
  assign RD1_17_0 = _1_18_sram_1_rd_1 | _1_18_sram_2_rd_1 | _1_18_sram_3_rd_1 | _1_18_sram_4_rd_1 | _1_18_sram_5_rd_1 | _1_18_sram_6_rd_1 | _1_18_sram_7_rd_1;  // Or or_1, 18 bits wide
  assign RD2_17_0 = _1_18_sram_1_rd_2 | _1_18_sram_2_rd_2 | _1_18_sram_3_rd_2 | _1_18_sram_4_rd_2 | _1_18_sram_5_rd_2 | _1_18_sram_6_rd_2 | _1_18_sram_7_rd_2;  // Or or_2, 18 bits wide
endmodule
