// Digital circuit Control Unit.dig as structural Verilog
module Control_Unit (
  input  [3:0] OP_3_0,
  input  ZF,
  input  SF,
  output [1:0] OP_1_0,
  output Im_sel,
  output Reg_EN,
  output JMP_SEL
);

  wire and_2_out, and_3_out, not_1_out, not_2_out, not_3_out, or_1_out, or_2_out;

  not not_1 (not_1_out, OP_3_0[3]);
  and and_1 (Im_sel, OP_3_0[2], not_1_out);
  not not_2 (not_2_out, SF);
  or or_1 (or_1_out, ZF, not_2_out);
  not not_3 (not_3_out, OP_3_0[2]);
  and and_2 (and_2_out, not_3_out, OP_3_0[3]);
  and and_3 (and_3_out, OP_3_0[2], OP_3_0[3]);
  and and_4 (JMP_SEL, and_2_out, or_1_out);
  or or_2 (or_2_out, and_2_out, and_3_out);
  not not_4 (Reg_EN, or_2_out);

  assign OP_1_0 = OP_3_0[1:0];
endmodule
