// Digital circuit SHL.dig as structural Verilog
module SHL (
  input  [4:0] A_4_0,
  input  [2:0] shift_3_0,
  output [4:0] O_4_0
);

  Multiplexer #(.Selector_Bits(3)) multiplexer_1 (
    .sel(shift_3_0), .in_0(A_4_0[4]), .in_1(A_4_0[3]), .in_2(A_4_0[2]), .in_3(A_4_0[1]), .in_4(A_4_0[0]),
    .in_5(1'b0), .in_6(1'b0), .in_7(1'b0), .out(O_4_0[4]));
  Multiplexer #(.Selector_Bits(3)) multiplexer_2 (
    .sel(shift_3_0), .in_0(A_4_0[3]), .in_1(A_4_0[2]), .in_2(A_4_0[1]), .in_3(A_4_0[0]), .in_4(1'b0),
    .in_5(1'b0), .in_6(1'b0), .in_7(1'b0), .out(O_4_0[3]));
  Multiplexer #(.Selector_Bits(3)) multiplexer_3 (
    .sel(shift_3_0), .in_0(A_4_0[2]), .in_1(A_4_0[1]), .in_2(A_4_0[0]), .in_3(1'b0), .in_4(1'b0),
    .in_5(1'b0), .in_6(1'b0), .in_7(1'b0), .out(O_4_0[2]));
  Multiplexer #(.Selector_Bits(3)) multiplexer_4 (
    .sel(shift_3_0), .in_0(A_4_0[1]), .in_1(A_4_0[0]), .in_2(1'b0), .in_3(1'b0), .in_4(1'b0), .in_5(1'b0),
    .in_6(1'b0), .in_7(1'b0), .out(O_4_0[1]));
  Multiplexer #(.Selector_Bits(3)) multiplexer_5 (
    .sel(shift_3_0), .in_0(A_4_0[0]), .in_1(1'b0), .in_2(1'b0), .in_3(1'b0), .in_4(1'b0), .in_5(1'b0),
    .in_6(1'b0), .in_7(1'b0), .out(O_4_0[0]));

  // Other names for the same wires on the sheet: A0 = A_4_0[0]; A1 = A_4_0[1]; A2 = A_4_0[2]; A3 = A_4_0[3];
  //   A4 = A_4_0[4]
endmodule
